# Fritzing sketch schematic (saved by Fritzing 0.9.3b)
breadboards: 1

parts:
  Part1 = Photon
  Part2 = HC-SR501 Body Sensor Module
  Part3 = 12 NeoPixel Ring [part_number=1643]

nets:
  N1: Part1.A4, Part2.OUT
  GND: Part1.GND, Part2.GND, Part3.GND
  VIN: Part1.VIN, Part2.VCC
  N2: Part1.D1, Part3.IN
  3V3: Part1.3V3, Part3.VDD

custom parts:
  HC-SR501 Body Sensor Module: Pyroelectric Infrared PIR Motion Sensor Detector Module
  12 NeoPixel Ring: 12 ultra bright smart LED NeoPixels are arranged in a circle with 1.5" (37mm) outer diameter. The rings are 'chainable' - connect the output pin of one to the input pin of another. Use only one microcontroller pin to control as many as you can chain together! Each LED is addressable as the driver chip is inside the LED. Each one has ~18mA constant current drive so the color will be very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
